# Fritzing sketch PrototypeConnection (saved by Fritzing 1.0.6)

parts:
  X1 = LilyGo TTGO LoRa32 T3 V1.6.1
  M1 = JSN-SRO4T [package=THT]
  YF-G1 = SEA YF-G1 Water Flow Sensor
  M2 = fc-51 [package=THT]
  Part1 = Barometric Pressure Sensor - BMP180 Breakout (GY-68)
  M3 = fc-51 [package=THT]
  M4 = fc-51 [package=THT]
  M5 = fc-51 [package=THT]

nets:
  N1: X1.GND#1, Part1.GND
  N2: X1.GND#2, M1.pin1, YF-G1.GND, M2.pin3, M3.pin3, M4.pin3, M5.pin3
  3V3: X1.3V3, Part1.VCC
  5V: X1.5V, M1.pin4, YF-G1.VCC, M2.pin1, M3.pin1, M4.pin1, M5.pin1
  N3: X1.34, M1.pin2
  N4: X1.35, M3.pin2
  N5: X1.12, M2.pin2
  N6: X1.25, YF-G1.Sig
  N7: X1.21, Part1.SDA
  N8: X1.22, Part1.SCL
  N9: X1.36, M5.pin2
  N10: X1.39, M4.pin2

notes:
  3
  2
  1
  0
  Bar02 Sensor

custom parts:
  LilyGo TTGO LoRa32 T3 V1.6.1: WSP32 based LoRaWAN Module with OLED
  JSN-SRO4T: JSN-SR04T Waterproof Ultrasonic Distance Measuring Module Integrated Ultrasonic Detection Module DC 5V.
  SEA YF-G1 Water Flow Sensor: YF-G1 Flow Sensor Input voltage 3.5V ~ 24V (DC), pulse rate 64.8/L
  fc-51: XKC-Y25-NPN Non-Contact Liquid Level Sensor IP67 Waterproof NPN Output Water Level Detector DC 5-12V.
